// Logisim project hack.circ as structural Verilog: 7 circuits, main circuit main
module main (
  input  in_1
);

  wire clock_1_out, cpu_1_writem;
  wire [14:0] cpu_1_addressm, cpu_1_pc;
  wire [15:0] cpu_1_outm, ram_1_data, rom_1_data;

  ROM #(.addrWidth(15), .dataWidth(16)) rom_1 (.addr(cpu_1_pc), .data(rom_1_data), .sel(1'b1));
  Clock clock_1 (.out(clock_1_out));
  CPU cpu_1 (
    .instruction(rom_1_data), .inM(ram_1_data), .reset(in_1), .writeM(cpu_1_writem), .outM(cpu_1_outm),
    .AddressM(cpu_1_addressm), .pc(cpu_1_pc), .clk(clock_1_out));
  RAM #(.addrWidth(15), .dataWidth(16), .bus("separate")) ram_1 (
    .addr(cpu_1_addressm), .din(cpu_1_outm), .data(ram_1_data), .str(cpu_1_writem), .sel(1'b1),
    .clk(clock_1_out), .ld(1'b1));  // open: clr

  // Notes on the sheet:
  //   Instruction Memory (ROM)
  //   contents of rom_1 (hex, n*v repeats v):
  //   9 ec10 0 e308 9 ec10 1 e308 2 ea88 0 fc98 14 e304 1 fc10 2 f088 a ea87 14 ea87
  //   Data Memory
endmodule

module CPU (
  input  [15:0] instruction,
  input  [15:0] inM,
  input  reset,
  input  clk,
  output writeM,
  output [15:0] outM,
  output [14:0] AddressM,
  output [14:0] pc
);

  wire alu_1_ng, alu_1_zr, decode_1_a, decode_1_i, not_1_out, or_1_out, pc_controller_1_inc,
       pc_controller_1_load;
  wire [2:0] decode_1_d, decode_1_j, multiplexer_1_out;
  wire [2:1] multiplexer_3_out;
  wire [5:0] decode_1_c, multiplexer_4_out;
  wire [15:0] A_q, D_q, multiplexer_2_out, multiplexer_5_out, pc_1_out;

  Decode decode_1 (
    .in_1(instruction), .i(decode_1_i), .a(decode_1_a), .c(decode_1_c), .d(decode_1_d), .j(decode_1_j));  // open: x
  Multiplexer #(.width(3), .enable("false")) multiplexer_1 (
    .in0(3'b000), .in1(decode_1_j), .out(multiplexer_1_out), .sel(decode_1_i));
  Multiplexer #(.width(16), .enable("false")) multiplexer_2 (
    .in0(instruction), .in1(outM), .out(multiplexer_2_out), .sel(decode_1_i));
  Multiplexer #(.width(3), .enable("false")) multiplexer_3 (
    .in0(3'b000), .in1(decode_1_d), .out({multiplexer_3_out, writeM}), .sel(decode_1_i));
  not not_1 (not_1_out, decode_1_i);
  or or_1 (or_1_out, not_1_out, multiplexer_3_out[2]);
  Register #(.width(16)) A (.D(multiplexer_2_out), .en(or_1_out), .Q(A_q), .clk(clk));  // open: clr
  Multiplexer #(.width(6), .enable("false")) multiplexer_4 (
    .in0({6{1'b0}}), .in1(decode_1_c), .out(multiplexer_4_out), .sel(decode_1_i));
  Register #(.width(16)) D (.D(outM), .en(multiplexer_3_out[1]), .Q(D_q), .clk(clk));  // open: clr
  Multiplexer #(.width(16), .enable("false")) multiplexer_5 (
    .in0(A_q), .in1(inM), .out(multiplexer_5_out), .sel(decode_1_a));
  ALU alu_1 (
    .x(multiplexer_5_out), .zx(multiplexer_4_out[3]), .nx(multiplexer_4_out[2]), .y(D_q),
    .zy(multiplexer_4_out[5]), .ny(multiplexer_4_out[4]), .f(multiplexer_4_out[1]),
    .no(multiplexer_4_out[0]), .out(outM), .zr(alu_1_zr), .ng(alu_1_ng));
  PC_Controller pc_controller_1 (
    .j0(multiplexer_1_out[2]), .j1(multiplexer_1_out[1]), .j2(multiplexer_1_out[0]), .zr(alu_1_ng),
    .ng(alu_1_zr), .load(pc_controller_1_load), .inc(pc_controller_1_inc));
  PC pc_1 (.in(A_q), .reset(reset), .load(pc_controller_1_load), .inc(pc_controller_1_inc), .clk(clk), .out(pc_1_out));
  BitSelector #(.width(16), .group(15)) bitselector_1 (.in(A_q), .out(AddressM), .sel(1'b0));
  BitSelector #(.width(16), .group(15)) bitselector_2 (.in(pc_1_out), .out(pc), .sel(1'b0));
endmodule

module ALU (
  input  [15:0] x,
  input  zx,
  input  nx,
  input  [15:0] y,
  input  zy,
  input  ny,
  input  f,
  input  no,
  output [15:0] out,
  output zr,
  output ng
);

  wire [15:0] adder_1_out, and_1_out, multiplexer_1_out, multiplexer_2_out, multiplexer_3_out,
       multiplexer_4_out, multiplexer_5_out, not_1_out, not_2_out, not_3_out;

  Multiplexer #(.width(16), .enable("false")) multiplexer_1 (
    .in0(x), .in1({16{1'b0}}), .out(multiplexer_1_out), .sel(zx));
  Multiplexer #(.width(16), .enable("false")) multiplexer_2 (
    .in0(y), .in1({16{1'b0}}), .out(multiplexer_2_out), .sel(zy));
  Multiplexer #(.width(16), .enable("false")) multiplexer_3 (
    .in0(multiplexer_1_out), .in1(not_1_out), .out(multiplexer_3_out), .sel(nx));
  assign not_1_out = ~multiplexer_1_out;  // NOT_Gate not_1, 16 bits wide
  Multiplexer #(.width(16), .enable("false")) multiplexer_4 (
    .in0(multiplexer_2_out), .in1(not_2_out), .out(multiplexer_4_out), .sel(ny));
  assign not_2_out = ~multiplexer_2_out;  // NOT_Gate not_2, 16 bits wide
  assign and_1_out = multiplexer_3_out & multiplexer_4_out;  // AND_Gate and_1, 16 bits wide
  Adder #(.width(16)) adder_1 (.a(multiplexer_3_out), .b(multiplexer_4_out), .out(adder_1_out));  // open: cin, cout
  Multiplexer #(.width(16), .enable("false")) multiplexer_5 (
    .in0(and_1_out), .in1(adder_1_out), .out(multiplexer_5_out), .sel(f));
  Multiplexer #(.width(16), .enable("false")) multiplexer_6 (
    .in0(multiplexer_5_out), .in1(not_3_out), .out(out), .sel(no));
  assign not_3_out = ~multiplexer_5_out;  // NOT_Gate not_3, 16 bits wide
  Comparator #(.width(16)) comparator_1 (.a(out), .b({16{1'b0}}), .eq(zr), .lt(ng));  // open: gt
endmodule

module Control_Logic (
);

  wire [15:0] undriven;

  Decode decode_1 (.in_1(undriven));  // open: i, x, a, c, d, j
endmodule

module Decode (
  input  [15:0] in_1,
  output i,
  output [1:0] x,
  output a,
  output [5:0] c,
  output [2:0] d,
  output [2:0] j
);


  assign a = in_1[12];
  assign c = in_1[11:6];
  assign d = in_1[5:3];
  assign i = in_1[15];
  assign j = in_1[2:0];
  assign x = in_1[14:13];
endmodule

module PC (
  input  [15:0] in,
  input  reset,
  input  load,
  input  inc,
  input  clk,
  output [15:0] out
);

  wire [15:0] adder_1_out, multiplexer_1_out, multiplexer_2_out, multiplexer_3_out;

  Multiplexer #(.width(16), .enable("false")) multiplexer_1 (
    .in0(out), .in1({16{1'b0}}), .out(multiplexer_1_out), .sel(reset));
  Multiplexer #(.width(16), .enable("false")) multiplexer_2 (
    .in0(multiplexer_1_out), .in1(in), .out(multiplexer_2_out), .sel(load));
  Multiplexer #(.width(16), .enable("false")) multiplexer_3 (
    .in0(multiplexer_2_out), .in1(adder_1_out), .out(multiplexer_3_out), .sel(inc));
  Adder #(.width(16)) adder_1 (.a(multiplexer_2_out), .b(16'h1), .out(adder_1_out));  // open: cin, cout
  Register #(.width(16)) register_1 (.D(multiplexer_3_out), .Q(out), .clk(clk));  // open: en, clr
endmodule

module PC_Controller (
  input  j0,
  input  j1,
  input  j2,
  input  zr,
  input  ng,
  output load,
  output inc
);

  wire and_1_out, and_2_out, and_3_out, and_4_out, not_1_out, not_2_out;

  not not_1 (not_1_out, zr);
  and and_1 (and_1_out, not_1_out, not_2_out);
  and and_2 (and_2_out, j1, ng);
  and and_3 (and_3_out, j0, zr);
  or or_1 (load, and_3_out, and_2_out, and_4_out);
  not not_2 (not_2_out, ng);
  and and_4 (and_4_out, and_1_out, j2);
  not not_3 (inc, load);
endmodule
