// Logisim project logisim.circ as structural Verilog
module ALU (
  input  [15:0] x,
  input  [15:0] y,
  input  zx,
  input  zy,
  input  nx,
  input  ny,
  input  f,
  input  no,
  output [15:0] out,
  output zr,
  output ng
);

  wire [15:0] adder_1_out, and_1_out, multiplexer_1_out, multiplexer_2_out, multiplexer_3_out,
       multiplexer_4_out, multiplexer_5_out, not_1_out, not_2_out, not_3_out;

  Multiplexer #(.width(16), .disabled(0), .enable("false")) multiplexer_1 (
    .in0(x), .in1({16{1'b0}}), .out(multiplexer_1_out), .sel(zx));
  assign not_1_out = ~multiplexer_1_out;  // NOT_Gate not_1, 16 bits wide
  Multiplexer #(.width(16), .disabled(0), .enable("false")) multiplexer_2 (
    .in0(multiplexer_1_out), .in1(not_1_out), .out(multiplexer_2_out), .sel(nx));
  assign and_1_out = multiplexer_2_out & multiplexer_4_out;  // AND_Gate and_1, 16 bits wide
  Multiplexer #(.width(16), .disabled(0), .enable("false")) multiplexer_3 (
    .in0(y), .in1({16{1'b0}}), .out(multiplexer_3_out), .sel(zy));
  assign not_2_out = ~multiplexer_3_out;  // NOT_Gate not_2, 16 bits wide
  Multiplexer #(.width(16), .disabled(0), .enable("false")) multiplexer_4 (
    .in0(multiplexer_3_out), .in1(not_2_out), .out(multiplexer_4_out), .sel(ny));
  Adder #(.width(16)) adder_1 (.a(multiplexer_4_out), .b(multiplexer_2_out), .out(adder_1_out));  // open: cin, cout
  Multiplexer #(.width(16), .disabled(0), .enable("false")) multiplexer_5 (
    .in0(and_1_out), .in1(adder_1_out), .out(multiplexer_5_out), .sel(f));
  assign not_3_out = ~multiplexer_5_out;  // NOT_Gate not_3, 16 bits wide
  Multiplexer #(.width(16), .disabled(0), .enable("false")) multiplexer_6 (
    .in0(multiplexer_5_out), .in1(not_3_out), .out(out), .sel(no));
  Comparator #(.width(16)) comparator_1 (.a(out), .b({16{1'b0}}), .eq(zr));  // open: gt, lt
  Comparator #(.width(16)) comparator_2 (.a(out), .b({16{1'b0}}), .lt(ng));  // open: gt, eq
endmodule

module CPU (
  input  [15:0] instruction,
  input  [15:0] inM,
  input  reset,
  input  clk,
  output [15:0] outM,
  output writeM,
  output [14:0] addressM,
  output [14:0] pc
);

  wire alu_1_ng, alu_1_zr, and_1_out, and_2_out, and_3_out, bitselector_1_out, bitselector_4_out, not_1_out,
       or_1_out;
  wire [2:0] j;
  wire [2:1] bitselector_3_out;
  wire [5:0] bitselector_5_out;
  wire [15:0] demultiplexer_1_out0, demultiplexer_1_out1, multiplexer_1_out, multiplexer_2_out, pc_1_out,
       register_1_q, register_2_q;

  BitSelector #(.width(16)) bitselector_1 (.in(instruction), .out(bitselector_1_out), .sel(4'b1111));
  Demultiplexer #(.width(16), .enable("false")) demultiplexer_1 (
    .out0(demultiplexer_1_out0), .out1(demultiplexer_1_out1), .in(instruction), .sel(bitselector_1_out));
  BitSelector #(.width(16), .group(3)) bitselector_2 (.in(demultiplexer_1_out0), .out(j), .sel(3'b000));
  Multiplexer #(.width(16), .enable("false")) multiplexer_1 (
    .in0(outM), .in1(instruction), .out(multiplexer_1_out), .sel(writeM));
  BitSelector #(.width(16), .group(3)) bitselector_3 (
    .in(demultiplexer_1_out1), .out({bitselector_3_out, writeM}), .sel(3'b001));
  Register #(.width(16)) register_1 (
    .D(multiplexer_1_out), .en(bitselector_3_out[2]), .Q(register_1_q), .clk(clk));  // open: clr
  BitSelector #(.width(16)) bitselector_4 (.in(demultiplexer_1_out1), .out(bitselector_4_out), .sel(4'b1101));
  Multiplexer #(.width(16), .enable("false")) multiplexer_2 (
    .in0(register_1_q), .in1(inM), .out(multiplexer_2_out), .sel(bitselector_4_out));
  Register #(.width(16)) register_2 (.D(outM), .en(bitselector_3_out[1]), .Q(register_2_q), .clk(clk));  // open: clr
  and and_1 (and_1_out, j[2], alu_1_ng);
  BitSelector #(.width(16), .group(6)) bitselector_5 (.in(demultiplexer_1_out1), .out(bitselector_5_out), .sel(2'b01));
  not not_1 (not_1_out, alu_1_ng);
  and and_2 (and_2_out, j[1], alu_1_zr);
  and and_3 (and_3_out, j[0], not_1_out);
  or or_1 (or_1_out, and_1_out, and_2_out, and_3_out);
  ALU alu_1 (
    .x(register_2_q), .y(multiplexer_2_out), .zx(bitselector_5_out[5]), .nx(bitselector_5_out[4]),
    .f(bitselector_5_out[1]), .no(bitselector_5_out[0]), .zy(bitselector_5_out[3]),
    .ny(bitselector_5_out[2]), .out(outM), .zr(alu_1_zr), .ng(alu_1_ng));
  PC pc_1 (.in(multiplexer_2_out), .load(or_1_out), .inc(1'b1), .reset(reset), .clk(clk), .out(pc_1_out));
  BitSelector #(.width(16), .group(15)) bitselector_6 (.in(multiplexer_2_out), .out(addressM), .sel(1'b0));
  BitSelector #(.width(16), .group(15)) bitselector_7 (.in(pc_1_out), .out(pc), .sel(1'b0));
endmodule

module Memory (
  input  [15:0] in,
  input  [14:0] address,
  input  clk,
  input  load,
  input  clear,
  input  [6:0] Tastatur
);

  wire demultiplexer_1_out0, demultiplexer_1_out1, demultiplexer_1_out2, demultiplexer_1_out3, or_1_out;
  wire [1:0] bitselector_2_out;
  wire [6:0] register_1_q;
  wire [11:0] bitselector_4_out;
  wire [12:0] bitselector_1_out;

  BitSelector #(.width(15), .group(13)) bitselector_1 (.in(address), .out(bitselector_1_out), .sel(1'b0));
  BitSelector #(.width(15)) bitselector_2 (.in(address), .out(bitselector_2_out[0]), .sel(4'b1101));
  BitSelector #(.width(15)) bitselector_3 (.in(address), .out(bitselector_2_out[1]), .sel(4'b1110));
  BitSelector #(.width(15), .group(12)) bitselector_4 (.in(address), .out(bitselector_4_out), .sel(1'b0));
  Demultiplexer #(.select(2), .enable("false")) demultiplexer_1 (
    .out0(demultiplexer_1_out0), .out1(demultiplexer_1_out1), .out2(demultiplexer_1_out2),
    .out3(demultiplexer_1_out3), .in(load), .sel(bitselector_2_out));
  Register #(.width(7)) register_1 (.D(Tastatur), .en(demultiplexer_1_out3), .Q(register_1_q), .clk(clk));  // open: clr
  or or_1 (or_1_out, demultiplexer_1_out1, demultiplexer_1_out0);
  assign in = {{9{1'b0}}, register_1_q};  // Bit_Extender bit_extender_1
  RAM #(.addrWidth(13), .dataWidth(16)) ram_1 (
    .addr(bitselector_1_out), .data(in), .sel(1'b1), .clk(clk), .ld(or_1_out), .clr(clear));
  RAM #(.addrWidth(12), .dataWidth(16)) ram_2 (
    .addr(bitselector_4_out), .data(in), .sel(1'b1), .clk(clk), .ld(demultiplexer_1_out2), .clr(clear));

  // Notes on the sheet:
  //   Ram16K
  //   Screen
  //   kann sein das hier ein delay entsteht
endmodule

module PC (
  input  [15:0] in,
  input  load,
  input  inc,
  input  reset,
  input  clk,
  output [15:0] out
);

  wire [15:0] adder_1_out, multiplexer_1_out, multiplexer_2_out;

  Multiplexer #(.width(16), .disabled(0), .enable("false")) multiplexer_1 (
    .in0(out), .in1(in), .out(multiplexer_1_out), .sel(load));
  Adder #(.width(16)) adder_1 (.a({16{1'b0}}), .b(multiplexer_1_out), .out(adder_1_out), .cin(1'b1));  // open: cout
  Multiplexer #(.width(16), .disabled(0), .enable("false")) multiplexer_2 (
    .in0(multiplexer_1_out), .in1(adder_1_out), .out(multiplexer_2_out), .sel(inc));
  Register #(.width(16)) register_1 (.D(multiplexer_2_out), .en(1'b1), .Q(out), .clk(clk), .clr(reset));
endmodule

module CPU2 (
  input  [15:0] instruction,
  input  [15:0] inM,
  input  reset,
  input  clk,
  output [15:0] outM,
  output writeM,
  output [14:0] addressM,
  output [14:0] pc
);

  wire undriven, undriven_2;
  wire [15:0] multiplexer_1_out, multiplexer_2_out, pc_1_out, register_1_q, register_2_q;

  Multiplexer #(.width(16), .enable("false")) multiplexer_1 (
    .in0(outM), .in1(instruction), .out(multiplexer_1_out));  // open: sel
  Register #(.width(16)) register_1 (.D(multiplexer_1_out), .en(undriven), .Q(register_1_q), .clk(clk));  // open: clr
  Multiplexer #(.width(16), .enable("false")) multiplexer_2 (
    .in0(register_1_q), .in1(inM), .out(multiplexer_2_out));  // open: sel
  Register #(.width(16)) register_2 (.D(outM), .Q(register_2_q), .clk(clk));  // open: en, clr
  ALU alu_1 ();  // open: x, y, zx, nx, f, no, zy, ny, out, zr, ng
  PC pc_1 (.in(multiplexer_2_out), .load(undriven_2), .inc(1'b1), .reset(reset), .clk(clk), .out(pc_1_out));
endmodule
